// Logisim project Assignment01.circ as structural Verilog: 4 circuits, main circuit main
module main (
  input  A,
  input  B,
  input  C,
  input  D,
  output out_5
);

  wire ic7404_not_1_out_8, ic7408_and_1_out_7, ic7408_and_1_out_8, ic7408_and_1_out_9;

  ic7404_NOT ic7404_not_1 (.in_4(D), .out_8(ic7404_not_1_out_8));  // open: in_1, in_2, in_3, out_5, out_6, out_7
  ic7408_AND ic7408_and_1 (
    .in_1(B), .in_2(ic7404_not_1_out_8), .in_3(C), .in_4(ic7404_not_1_out_8), .in_5(ic7404_not_1_out_8),
    .in_6(A), .out_7(ic7408_and_1_out_7), .out_8(ic7408_and_1_out_8), .out_9(ic7408_and_1_out_9));
  ic4075_OR ic4075_or_1 (
    .in_1(ic7408_and_1_out_8), .in_2(ic7408_and_1_out_7), .in_3(ic7408_and_1_out_9), .out_4(out_5));

  // Notes on the sheet:
  //   D'
  //   A
  //   B
  //   Assignment01
  //    Team45
  //   C
  //   D'
  //   D'
  //   BD'
  //   CD'
  //   AD'
  //   F= AD' + BD' + CD'
endmodule

module ic7408_AND (
  input  in_1,
  input  in_2,
  input  in_3,
  input  in_4,
  input  in_5,
  input  in_6,
  output out_7,
  output out_8,
  output out_9
);

  and and_1 (out_7, in_1, in_2);
  and and_2 (out_8, in_3, in_4);
  and and_3 (out_9, in_5, in_6);
endmodule

module ic7404_NOT (
  input  in_1,
  input  in_2,
  input  in_3,
  input  in_4,
  output out_5,
  output out_6,
  output out_7,
  output out_8
);

  not not_1 (out_5, in_1);
  not not_2 (out_6, in_2);
  not not_3 (out_7, in_3);
  not not_4 (out_8, in_4);
endmodule

module ic4075_OR (
  input  in_1,
  input  in_2,
  input  in_3,
  output out_4
);

  or or_1 (out_4, in_1, in_2, in_3);
endmodule
