// Logisim project lab2 d1.circ as structural Verilog: 1 circuit, main circuit main
module main (
  input  in_1,
  input  in_2,
  input  in_3,
  input  in_4,
  input  in_5,
  input  in_6,
  input  in_7,
  input  in_8,
  input  in_9,
  input  in_10,
  input  in_11,
  input  in_12,
  input  in_13,
  output out_14,
  output out_15,
  output out_16,
  output out_17,
  output out_18,
  output out_19
);

  wire nand_1_out, nand_2_out, NAND_3_out;

  nand nand_1 (nand_1_out, in_10, in_11);
  nand nand_2 (nand_2_out, in_12, in_13);
  and AND (out_14, in_1, in_2);
  nand NAND_3 (NAND_3_out, in_3, in_4);
  not not_1 (out_16, in_5);
  nand NAND_4 (out_17, in_6, in_7);
  or or_1 (out_18, in_8, in_9);
  nand NAND_5 (out_15, NAND_3_out, NAND_3_out);
  nand nand_6 (out_19, nand_1_out, nand_2_out);

  // Notes on the sheet:
  //   NOT
endmodule
