// Logisim project lab2 d3.circ as structural Verilog: 4 circuits, main circuit main
module main (
  input  a,
  input  b,
  input  c,
  output out_4
);

  wire and_1_out_5, and_1_out_6, not_1_out_2;

  \and  and_1 (.in_1(not_1_out_2), .in_2(b), .out_5(and_1_out_5), .in_3(c), .in_4(a), .out_6(and_1_out_6));
  \not  not_1 (.in_1(c), .out_2(not_1_out_2));
  \or  or_1 (.in_1(and_1_out_6), .in_2(and_1_out_5), .out_3(out_4));

  // Notes on the sheet:
  //   c
  //   a
  //   b
  //   c'
  //   ac
  //   bc'
endmodule

module \and  (
  input  in_1,
  input  in_2,
  input  in_3,
  input  in_4,
  output out_5,
  output out_6
);

  wire nand_1_out, nand_2_out;

  nand nand_1 (nand_1_out, in_1, in_2);
  nand nand_2 (nand_2_out, in_3, in_4);
  nand nand_3 (out_5, nand_1_out, nand_1_out);
  nand nand_4 (out_6, nand_2_out, nand_2_out);
endmodule

module \or  (
  input  in_1,
  input  in_2,
  output out_3
);

  wire nand_1_out, nand_2_out;

  nand nand_1 (nand_1_out, in_1, in_1);
  nand nand_2 (nand_2_out, in_2, in_2);
  nand nand_3 (out_3, nand_1_out, nand_2_out);
endmodule

module \not  (
  input  in_1,
  output out_2
);

  nand nand_1 (out_2, in_1, in_1);
endmodule
