// Logisim project lab4.circ as structural Verilog: 5 circuits, main circuit main
module main (
  input  w,
  input  x,
  input  y,
  input  z,
  output A___W___XZ___XY,
  output out_6,
  output C___Y_prime_Z_prime___YZ,
  output D___Z_prime
);

  wire ic7404_not_1_out_11, ic7404_not_1_out_12, n7408_and_1_out_9, n7408_and_1_out_10, n7408_and_1_out_11,
       n7408_and_1_out_12, n7408_and_2_out_11, n7408_and_2_out_12, n7411_and_1_out_12;

  ic7404_NOT ic7404_not_1 (
    .in_4(z), .in_5(y), .in_6(x), .out_10(D___Z_prime), .out_11(ic7404_not_1_out_11),
    .out_12(ic7404_not_1_out_12));  // open: in_1, in_2, in_3, out_7, out_8, out_9
  _7408_AND u_7408_and_1 (
    .in_1(ic7404_not_1_out_12), .in_2(z), .in_3(ic7404_not_1_out_12), .in_4(y), .in_5(y), .in_6(x), .in_7(z),
    .in_8(x), .out_9(n7408_and_1_out_9), .out_10(n7408_and_1_out_10), .out_11(n7408_and_1_out_11),
    .out_12(n7408_and_1_out_12));
  _7411_AND u_7411_and_1 (
    .in_7(D___Z_prime), .in_8(ic7404_not_1_out_11), .in_9(x), .out_12(n7411_and_1_out_12));  // open: in_1, in_2, in_3, in_4, in_5, in_6, out_10, out_11
  ic_4075_OR ic_4075_or_1 (
    .in_1(n7408_and_1_out_9), .in_2(n7408_and_1_out_10), .in_3(n7411_and_1_out_12),
    .in_4(n7408_and_2_out_12), .in_5(n7408_and_2_out_11), .in_7(n7408_and_1_out_11),
    .in_8(n7408_and_1_out_12), .in_9(w), .out_10(out_6), .out_11(C___Y_prime_Z_prime___YZ),
    .out_12(A___W___XZ___XY));  // open: in_6
  _7408_AND u_7408_and_2 (
    .in_5(y), .in_6(z), .in_7(ic7404_not_1_out_11), .in_8(D___Z_prime), .out_11(n7408_and_2_out_11),
    .out_12(n7408_and_2_out_12));  // open: in_1, in_2, in_3, in_4, out_9, out_10

  // Notes on the sheet:
  //   Y
  //   Z
  //   X
  //   W
  //   Z'
  //   Y'
  //   X'
  //   XY
  //   XZ
  //   X'Y
  //   X'Z
  //   XY'Z'
  //   Z'
  //   YZ
  //   B = X'Z + X'Y + XY'Z'
  //   Y'Z'
endmodule

module ic7404_NOT (
  input  in_1,
  input  in_2,
  input  in_3,
  input  in_4,
  input  in_5,
  input  in_6,
  output out_7,
  output out_8,
  output out_9,
  output out_10,
  output out_11,
  output out_12
);

  not not_1 (out_7, in_1);
  not not_2 (out_8, in_2);
  not not_3 (out_9, in_3);
  not not_4 (out_10, in_4);
  not not_5 (out_11, in_5);
  not not_6 (out_12, in_6);
endmodule

module ic_4075_OR (
  input  in_1,
  input  in_2,
  input  in_3,
  input  in_4,
  input  in_5,
  input  in_6,
  input  in_7,
  input  in_8,
  input  in_9,
  output out_10,
  output out_11,
  output out_12
);

  or or_1 (out_10, in_1, in_2, in_3);
  or or_2 (out_11, in_4, in_5, in_6);
  or or_3 (out_12, in_7, in_8, in_9);
endmodule

module _7411_AND (
  input  in_1,
  input  in_2,
  input  in_3,
  input  in_4,
  input  in_5,
  input  in_6,
  input  in_7,
  input  in_8,
  input  in_9,
  output out_10,
  output out_11,
  output out_12
);

  and and_1 (out_10, in_1, in_2, in_3);
  and and_2 (out_11, in_4, in_5, in_6);
  and and_3 (out_12, in_7, in_8, in_9);
endmodule

module _7408_AND (
  input  in_1,
  input  in_2,
  input  in_3,
  input  in_4,
  input  in_5,
  input  in_6,
  input  in_7,
  input  in_8,
  output out_9,
  output out_10,
  output out_11,
  output out_12
);

  and and_1 (out_9, in_1, in_2);
  and and_2 (out_10, in_3, in_4);
  and and_3 (out_11, in_5, in_6);
  and and_4 (out_12, in_7, in_8);
endmodule
