// Logisim project lab5.1.circ as structural Verilog: 3 circuits, main circuit main
module main (
  input  in_1,
  input  in_2,
  input  in_3,
  input  in_4,
  input  in_5,
  input  in_6,
  input  in_7,
  input  in_8,
  input  in_9,
  output [3:0] out_10,
  output out_11
);

  wire ic7486_xor_1_out_9, ic7486_xor_1_out_10, ic7486_xor_1_out_11, ic7486_xor_1_out_12;

  ic7486_xor ic7486_xor_1 (
    .in_1(in_9), .in_2(in_8), .in_3(in_9), .in_4(in_7), .in_5(in_6), .in_6(in_9), .in_7(in_5), .in_8(in_9),
    .out_9(ic7486_xor_1_out_9), .out_10(ic7486_xor_1_out_10), .out_11(ic7486_xor_1_out_11),
    .out_12(ic7486_xor_1_out_12));
  ic74283_adder ic74283_adder_1 (
    .in_2(in_1), .in_3(ic7486_xor_1_out_12), .in_4(in_2), .in_5(ic7486_xor_1_out_11), .in_6(in_3),
    .in_7(ic7486_xor_1_out_10), .in_8(in_4), .in_9(ic7486_xor_1_out_9), .out_10(out_10), .out_11(out_11),
    .in_1(in_9));
endmodule

module ic7486_xor (
  input  in_1,
  input  in_2,
  input  in_3,
  input  in_4,
  input  in_5,
  input  in_6,
  input  in_7,
  input  in_8,
  output out_9,
  output out_10,
  output out_11,
  output out_12
);

  xor xor_1 (out_9, in_1, in_2);
  xor xor_2 (out_10, in_3, in_4);
  xor xor_3 (out_11, in_5, in_6);
  xor xor_4 (out_12, in_7, in_8);
endmodule

module ic74283_adder (
  input  in_1,
  input  in_2,
  input  in_3,
  input  in_4,
  input  in_5,
  input  in_6,
  input  in_7,
  input  in_8,
  input  in_9,
  output [3:0] out_10,
  output out_11
);

  wire adder_1_cout, adder_2_cout, adder_3_cout;

  Adder #(.width(1)) adder_1 (.a(in_2), .b(in_3), .out(out_10[0]), .cin(in_1), .cout(adder_1_cout));
  Adder #(.width(1)) adder_2 (.a(in_4), .b(in_5), .out(out_10[1]), .cin(adder_1_cout), .cout(adder_2_cout));
  Adder #(.width(1)) adder_3 (.a(in_6), .b(in_7), .out(out_10[2]), .cin(adder_2_cout), .cout(adder_3_cout));
  Adder #(.width(1)) adder_4 (.a(in_8), .b(in_9), .out(out_10[3]), .cin(adder_3_cout), .cout(out_11));
endmodule
