// Logisim project lab5.2.circ as structural Verilog: 4 circuits, main circuit main
module main (
  input  in_1,
  input  in_2,
  input  in_3,
  input  in_4,
  input  in_5,
  input  in_6,
  input  in_7,
  input  in_8,
  input  in_9,
  input  in_10,
  input  in_11,
  output out_12,
  output out_13,
  output out_14,
  output out_15,
  output out_16,
  output out_17
);

  wire n7408_and_1_out_9, n7408_and_1_out_10, n7432_or_1_out_12, n74283_adder_1_out_10,
       n74283_adder_1_out_11, n74283_adder_1_out_12, n74283_adder_1_out_13, n74283_adder_1_out_14, undriven,
       undriven_2;

  _7432_or u_7432_or_1 (
    .in_1(n74283_adder_1_out_14), .in_2(n7432_or_1_out_12), .in_7(n7408_and_1_out_9),
    .in_8(n7408_and_1_out_10), .out_9(out_17), .out_12(n7432_or_1_out_12));  // open: in_3, in_4, in_5, in_6, out_10, out_11
  _74283_adder u_74283_adder_1 (
    .in_1(undriven), .in_2(in_6), .in_3(in_2), .in_4(in_7), .in_5(in_3), .in_6(in_8), .in_7(in_4),
    .in_8(in_9), .in_9(in_5), .out_14(n74283_adder_1_out_14), .out_10(n74283_adder_1_out_10),
    .out_11(n74283_adder_1_out_11), .out_12(n74283_adder_1_out_12), .out_13(n74283_adder_1_out_13));
  _7408_and u_7408_and_1 (
    .in_1(n74283_adder_1_out_12), .in_2(n74283_adder_1_out_13), .in_3(n74283_adder_1_out_11),
    .in_4(n74283_adder_1_out_13), .out_9(n7408_and_1_out_9), .out_10(n7408_and_1_out_10));  // open: in_5, in_6, in_7, in_8, out_11, out_12
  _74283_adder u_74283_adder_2 (
    .in_1(undriven_2), .in_2(in_1), .in_3(n74283_adder_1_out_10), .in_4(in_1), .in_5(n74283_adder_1_out_11),
    .in_6(out_17), .in_7(n74283_adder_1_out_12), .in_8(out_17), .in_9(n74283_adder_1_out_13),
    .out_14(out_16), .out_10(out_12), .out_11(out_13), .out_12(out_14), .out_13(out_15));

  // Notes on the sheet:
  //   b
  //   a
endmodule

module _7432_or (
  input  in_1,
  input  in_2,
  input  in_3,
  input  in_4,
  input  in_5,
  input  in_6,
  input  in_7,
  input  in_8,
  output out_9,
  output out_10,
  output out_11,
  output out_12
);

  or or_1 (out_9, in_1, in_2);
  or or_2 (out_10, in_3, in_4);
  or or_3 (out_11, in_5, in_6);
  or or_4 (out_12, in_7, in_8);
endmodule

module _7408_and (
  input  in_1,
  input  in_2,
  input  in_3,
  input  in_4,
  input  in_5,
  input  in_6,
  input  in_7,
  input  in_8,
  output out_9,
  output out_10,
  output out_11,
  output out_12
);

  and and_1 (out_9, in_1, in_2);
  and and_2 (out_10, in_3, in_4);
  and and_3 (out_11, in_5, in_6);
  and and_4 (out_12, in_7, in_8);
endmodule

module _74283_adder (
  input  in_1,
  input  in_2,
  input  in_3,
  input  in_4,
  input  in_5,
  input  in_6,
  input  in_7,
  input  in_8,
  input  in_9,
  output out_10,
  output out_11,
  output out_12,
  output out_13,
  output out_14
);

  wire adder_1_cout, adder_2_cout, adder_3_cout;

  Adder #(.width(1)) adder_1 (.a(in_2), .b(in_3), .out(out_10), .cin(in_1), .cout(adder_1_cout));
  Adder #(.width(1)) adder_2 (.a(in_4), .b(in_5), .out(out_11), .cin(adder_1_cout), .cout(adder_2_cout));
  Adder #(.width(1)) adder_3 (.a(in_6), .b(in_7), .out(out_12), .cin(adder_2_cout), .cout(adder_3_cout));
  Adder #(.width(1)) adder_4 (.a(in_8), .b(in_9), .out(out_13), .cin(adder_3_cout), .cout(out_14));
endmodule
